// Logisim project P3.circ as structural Verilog: 6 circuits, main circuit BIT
// Bit
module BIT (
  input  CLOCK,
  input  IN,
  input  LOAD,
  output out_4
);

  wire multiplexer_1_out;

  Multiplexer multiplexer_1 (.in0(out_4), .in1(IN), .out(multiplexer_1_out), .sel(LOAD));  // open: en
  D_Flip_Flop u_IN (.clk(CLOCK), .D(multiplexer_1_out), .Q(out_4));  // open: Qn, preset, en, reset
endmodule

module REGISTER (
  input  CLOCK,
  input  LOAD,
  input  [15:0] IN,
  output [15:0] out_4
);

  BIT bit_1 (.CLOCK(CLOCK), .IN(IN[0]), .LOAD(LOAD), .out_4(out_4[0]));
  BIT bit_2 (.CLOCK(CLOCK), .IN(IN[1]), .LOAD(LOAD), .out_4(out_4[1]));
  BIT bit_3 (.CLOCK(CLOCK), .IN(IN[2]), .LOAD(LOAD), .out_4(out_4[2]));
  BIT bit_4 (.CLOCK(CLOCK), .IN(IN[3]), .LOAD(LOAD), .out_4(out_4[3]));
  BIT bit_5 (.CLOCK(CLOCK), .IN(IN[4]), .LOAD(LOAD), .out_4(out_4[4]));
  BIT bit_6 (.CLOCK(CLOCK), .IN(IN[5]), .LOAD(LOAD), .out_4(out_4[5]));
  BIT bit_7 (.CLOCK(CLOCK), .IN(IN[6]), .LOAD(LOAD), .out_4(out_4[6]));
  BIT bit_8 (.CLOCK(CLOCK), .IN(IN[7]), .LOAD(LOAD), .out_4(out_4[7]));
  BIT bit_9 (.CLOCK(CLOCK), .IN(IN[8]), .LOAD(LOAD), .out_4(out_4[8]));
  BIT bit_10 (.CLOCK(CLOCK), .IN(IN[9]), .LOAD(LOAD), .out_4(out_4[9]));
  BIT bit_11 (.CLOCK(CLOCK), .IN(IN[10]), .LOAD(LOAD), .out_4(out_4[10]));
  BIT bit_12 (.CLOCK(CLOCK), .IN(IN[11]), .LOAD(LOAD), .out_4(out_4[11]));
  BIT bit_13 (.CLOCK(CLOCK), .IN(IN[12]), .LOAD(LOAD), .out_4(out_4[12]));
  BIT bit_14 (.CLOCK(CLOCK), .IN(IN[13]), .LOAD(LOAD), .out_4(out_4[13]));
  BIT bit_15 (.CLOCK(CLOCK), .IN(IN[14]), .LOAD(LOAD), .out_4(out_4[14]));
  BIT bit_16 (.CLOCK(CLOCK), .IN(IN[15]), .LOAD(LOAD), .out_4(out_4[15]));
endmodule

module RAM8 (
  input  clock,
  input  load,
  input  [15:0] IN,
  input  [2:0] address,
  output [15:0] out_5
);

  wire demultiplexer_1_out0, demultiplexer_1_out1, demultiplexer_1_out2, demultiplexer_1_out3,
       demultiplexer_1_out4, demultiplexer_1_out5, demultiplexer_1_out6, demultiplexer_1_out7;
  wire [15:0] register_1_out_4, register_2_out_4, register_3_out_4, register_4_out_4, register_5_out_4,
       register_6_out_4, register_7_out_4, register_8_out_4;

  Demultiplexer #(.select(3), .enable("false")) demultiplexer_1 (
    .out0(demultiplexer_1_out0), .out1(demultiplexer_1_out1), .out2(demultiplexer_1_out2),
    .out3(demultiplexer_1_out3), .out4(demultiplexer_1_out4), .out5(demultiplexer_1_out5),
    .out6(demultiplexer_1_out6), .out7(demultiplexer_1_out7), .in(load), .sel(address));
  REGISTER register_1 (.CLOCK(clock), .LOAD(demultiplexer_1_out0), .IN(IN), .out_4(register_1_out_4));
  REGISTER register_2 (.CLOCK(clock), .LOAD(demultiplexer_1_out1), .IN(IN), .out_4(register_2_out_4));
  REGISTER register_3 (.CLOCK(clock), .LOAD(demultiplexer_1_out2), .IN(IN), .out_4(register_3_out_4));
  REGISTER register_4 (.CLOCK(clock), .LOAD(demultiplexer_1_out3), .IN(IN), .out_4(register_4_out_4));
  REGISTER register_5 (.CLOCK(clock), .LOAD(demultiplexer_1_out4), .IN(IN), .out_4(register_5_out_4));
  REGISTER register_6 (.CLOCK(clock), .LOAD(demultiplexer_1_out5), .IN(IN), .out_4(register_6_out_4));
  REGISTER register_7 (.CLOCK(clock), .LOAD(demultiplexer_1_out6), .IN(IN), .out_4(register_7_out_4));
  REGISTER register_8 (.CLOCK(clock), .LOAD(demultiplexer_1_out7), .IN(IN), .out_4(register_8_out_4));
  Multiplexer #(.select(3), .width(16), .enable("false")) multiplexer_1 (
    .in0(register_1_out_4), .in1(register_2_out_4), .in2(register_3_out_4), .in3(register_4_out_4),
    .in4(register_5_out_4), .in5(register_6_out_4), .in6(register_7_out_4), .in7(register_8_out_4),
    .out(out_5), .sel(address));
endmodule

module RAM64 (
  input  CLOCK,
  input  LOAD,
  input  [15:0] IN,
  input  [5:0] ADDRESS,
  output [15:0] out_5
);

  wire demultiplexer_1_out0, demultiplexer_1_out1, demultiplexer_1_out2, demultiplexer_1_out3,
       demultiplexer_1_out4, demultiplexer_1_out5, demultiplexer_1_out6, demultiplexer_1_out7;
  wire [15:0] ram8_1_out_5, ram8_2_out_5, ram8_3_out_5, ram8_4_out_5, ram8_5_out_5, ram8_6_out_5,
       ram8_7_out_5, ram8_8_out_5;

  Demultiplexer #(.select(3), .enable("false")) demultiplexer_1 (
    .out0(demultiplexer_1_out0), .out1(demultiplexer_1_out1), .out2(demultiplexer_1_out2),
    .out3(demultiplexer_1_out3), .out4(demultiplexer_1_out4), .out5(demultiplexer_1_out5),
    .out6(demultiplexer_1_out6), .out7(demultiplexer_1_out7), .in(LOAD), .sel(ADDRESS[5:3]));
  RAM8 ram8_1 (.clock(CLOCK), .load(demultiplexer_1_out0), .IN(IN), .address(ADDRESS[2:0]), .out_5(ram8_1_out_5));
  RAM8 ram8_2 (.clock(CLOCK), .load(demultiplexer_1_out1), .IN(IN), .address(ADDRESS[2:0]), .out_5(ram8_2_out_5));
  RAM8 ram8_3 (.clock(CLOCK), .load(demultiplexer_1_out2), .IN(IN), .address(ADDRESS[2:0]), .out_5(ram8_3_out_5));
  RAM8 ram8_4 (.clock(CLOCK), .load(demultiplexer_1_out3), .IN(IN), .address(ADDRESS[2:0]), .out_5(ram8_4_out_5));
  RAM8 ram8_5 (.clock(CLOCK), .load(demultiplexer_1_out4), .IN(IN), .address(ADDRESS[2:0]), .out_5(ram8_5_out_5));
  RAM8 ram8_6 (.clock(CLOCK), .load(demultiplexer_1_out5), .IN(IN), .address(ADDRESS[2:0]), .out_5(ram8_6_out_5));
  RAM8 ram8_7 (.clock(CLOCK), .load(demultiplexer_1_out6), .IN(IN), .address(ADDRESS[2:0]), .out_5(ram8_7_out_5));
  RAM8 ram8_8 (.clock(CLOCK), .load(demultiplexer_1_out7), .IN(IN), .address(ADDRESS[2:0]), .out_5(ram8_8_out_5));
  Multiplexer #(.select(3), .width(16), .enable("false")) multiplexer_1 (
    .in0(ram8_1_out_5), .in1(ram8_2_out_5), .in2(ram8_3_out_5), .in3(ram8_4_out_5), .in4(ram8_5_out_5),
    .in5(ram8_6_out_5), .in6(ram8_7_out_5), .in7(ram8_8_out_5), .out(out_5), .sel(ADDRESS[5:3]));

  // Other names for the same wires on the sheet: ADR[2:0] = ADDRESS[2:0]
endmodule

module RAM512 (
  input  LOAD,
  input  [15:0] IN,
  input  [8:0] ADDRESS,
  output [15:0] out_4
);

  wire clock_1_out, demultiplexer_1_out0, demultiplexer_1_out1, demultiplexer_1_out2, demultiplexer_1_out3,
       demultiplexer_1_out4, demultiplexer_1_out5, demultiplexer_1_out6, demultiplexer_1_out7;
  wire [15:0] ram64_1_out_5, ram64_2_out_5, ram64_3_out_5, ram64_4_out_5, ram64_5_out_5, ram64_6_out_5,
       ram64_7_out_5, ram64_8_out_5;

  Clock clock_1 (.out(clock_1_out));
  Demultiplexer #(.select(3), .enable("false")) demultiplexer_1 (
    .out0(demultiplexer_1_out0), .out1(demultiplexer_1_out1), .out2(demultiplexer_1_out2),
    .out3(demultiplexer_1_out3), .out4(demultiplexer_1_out4), .out5(demultiplexer_1_out5),
    .out6(demultiplexer_1_out6), .out7(demultiplexer_1_out7), .in(LOAD), .sel(ADDRESS[8:6]));
  RAM64 ram64_1 (
    .CLOCK(clock_1_out), .LOAD(demultiplexer_1_out0), .IN(IN), .ADDRESS(ADDRESS[5:0]), .out_5(ram64_1_out_5));
  RAM64 ram64_2 (
    .CLOCK(clock_1_out), .LOAD(demultiplexer_1_out1), .IN(IN), .ADDRESS(ADDRESS[5:0]), .out_5(ram64_2_out_5));
  RAM64 ram64_3 (
    .CLOCK(clock_1_out), .LOAD(demultiplexer_1_out2), .IN(IN), .ADDRESS(ADDRESS[5:0]), .out_5(ram64_3_out_5));
  RAM64 ram64_4 (
    .CLOCK(clock_1_out), .LOAD(demultiplexer_1_out3), .IN(IN), .ADDRESS(ADDRESS[5:0]), .out_5(ram64_4_out_5));
  RAM64 ram64_5 (
    .CLOCK(clock_1_out), .LOAD(demultiplexer_1_out4), .IN(IN), .ADDRESS(ADDRESS[5:0]), .out_5(ram64_5_out_5));
  RAM64 ram64_6 (
    .CLOCK(clock_1_out), .LOAD(demultiplexer_1_out5), .IN(IN), .ADDRESS(ADDRESS[5:0]), .out_5(ram64_6_out_5));
  RAM64 ram64_7 (
    .CLOCK(clock_1_out), .LOAD(demultiplexer_1_out6), .IN(IN), .ADDRESS(ADDRESS[5:0]), .out_5(ram64_7_out_5));
  RAM64 ram64_8 (
    .CLOCK(clock_1_out), .LOAD(demultiplexer_1_out7), .IN(IN), .ADDRESS(ADDRESS[5:0]), .out_5(ram64_8_out_5));
  Multiplexer #(.select(3), .width(16), .enable("false")) multiplexer_1 (
    .in0(ram64_1_out_5), .in1(ram64_2_out_5), .in2(ram64_3_out_5), .in3(ram64_4_out_5), .in4(ram64_5_out_5),
    .in5(ram64_6_out_5), .in6(ram64_7_out_5), .in7(ram64_8_out_5), .out(out_4), .sel(ADDRESS[8:6]));
endmodule

module RAM4K (
  input  LOAD,
  input  [15:0] IN,
  input  [11:0] ADDRESS
);

  wire demultiplexer_1_out0, demultiplexer_1_out1, demultiplexer_1_out2, demultiplexer_1_out3,
       demultiplexer_1_out4, demultiplexer_1_out5, demultiplexer_1_out6, demultiplexer_1_out7;

  Demultiplexer #(.select(3), .enable("false")) demultiplexer_1 (
    .out0(demultiplexer_1_out0), .out1(demultiplexer_1_out1), .out2(demultiplexer_1_out2),
    .out3(demultiplexer_1_out3), .out4(demultiplexer_1_out4), .out5(demultiplexer_1_out5),
    .out6(demultiplexer_1_out6), .out7(demultiplexer_1_out7), .in(LOAD), .sel(ADDRESS[11:9]));
  RAM512 ram512_1 (.LOAD(demultiplexer_1_out0));  // open: IN, ADDRESS, out_4
  RAM512 ram512_2 (.LOAD(demultiplexer_1_out1));  // open: IN, ADDRESS, out_4
  RAM512 ram512_3 (.LOAD(demultiplexer_1_out2));  // open: IN, ADDRESS, out_4
  RAM512 ram512_4 (.LOAD(demultiplexer_1_out3));  // open: IN, ADDRESS, out_4
  RAM512 ram512_5 (.LOAD(demultiplexer_1_out4));  // open: IN, ADDRESS, out_4
  RAM512 ram512_6 (.LOAD(demultiplexer_1_out5));  // open: IN, ADDRESS, out_4
  RAM512 ram512_7 (.LOAD(demultiplexer_1_out6));  // open: IN, ADDRESS, out_4
  RAM512 ram512_8 (.LOAD(demultiplexer_1_out7));  // open: IN, ADDRESS, out_4
endmodule
